// Logisim project realALU.circ as structural Verilog
module AND (
  input  Enable,
  input  [7:0] inA,
  input  [7:0] inB,
  output [7:0] out,
  output Z__1_if_out____0x00
);

  wire [7:0] and_1_out;

  assign and_1_out = inA & inB;  // AND_Gate and_1, 8 bits wide
  Transistor #(.\type ("n"), .width(8)) transistor_1 (.in(and_1_out), .out(out), .gate(Enable));
  Pull_Resistor pull_resistor_1 (.node(out));
  nor nor_1 (Z__1_if_out____0x00, and_1_out[0], and_1_out[1], and_1_out[2], and_1_out[3], and_1_out[4], and_1_out[5], and_1_out[6], and_1_out[7]);
endmodule

module OR (
  input  Enable,
  input  [7:0] inA,
  input  [7:0] inB,
  output [7:0] out,
  output Z__1_if_out____0x00
);

  wire [7:0] or_1_out;

  assign or_1_out = inA | inB;  // OR_Gate or_1, 8 bits wide
  Transistor #(.\type ("n"), .width(8)) transistor_1 (.in(or_1_out), .out(out), .gate(Enable));
  Pull_Resistor pull_resistor_1 (.node(out));
  nor nor_1 (Z__1_if_out____0x00, or_1_out[0], or_1_out[1], or_1_out[2], or_1_out[3], or_1_out[4], or_1_out[5], or_1_out[6], or_1_out[7]);
endmodule

module NOT (
  input  Enable,
  input  [7:0] in,
  output [7:0] out,
  output Z__1_if_out____0x00
);

  wire [7:0] not_1_out;

  assign not_1_out = ~in;  // NOT_Gate not_1, 8 bits wide
  Pull_Resistor pull_resistor_1 (.node(out));
  Transistor #(.\type ("n"), .width(8)) transistor_1 (.in(not_1_out), .out(out), .gate(Enable));
  nor nor_1 (Z__1_if_out____0x00, not_1_out[0], not_1_out[1], not_1_out[2], not_1_out[3], not_1_out[4], not_1_out[5], not_1_out[6], not_1_out[7]);
endmodule

module logicalShiftRight (
  input  Enable,
  input  [7:0] in,
  output [7:0] out,
  output Z__1_if_out____0x00,
  output C__1_if_out__1_____1,
  output N__1_if_out_7_____1
);

  Pull_Resistor pull_resistor_1 (.node(out));
  Transistor #(.\type ("n"), .width(8)) transistor_1 (.in({1'b0, in[7:1]}), .out(out), .gate(Enable));
  nor nor_1 (Z__1_if_out____0x00, in[1], in[2], in[3], in[4], in[5], in[6], in[7], 1'b0);

  assign C__1_if_out__1_____1 = in[0];
  assign N__1_if_out_7_____1 = 1'b0;

  // Other names for the same wires on the sheet: C = in[0]
endmodule

module logicalShiftLeft (
  input  Enable,
  input  [7:0] in,
  output [7:0] out,
  output Z__1_if_out____0x00,
  output C__1_if_out_8_____1,
  output N__1_if_out_7_____1
);

  Pull_Resistor pull_resistor_1 (.node(out));
  Transistor #(.\type ("n"), .width(8)) transistor_1 (.in({in[6:0], 1'b0}), .out(out), .gate(Enable));
  nor nor_1 (Z__1_if_out____0x00, 1'b0, in[0], in[1], in[2], in[3], in[4], in[5], in[6]);

  assign C__1_if_out_8_____1 = in[7];
  assign N__1_if_out_7_____1 = in[6];

  // Other names for the same wires on the sheet: C = in[7]
endmodule

module decoder8 (
  input  Enable,
  input  [2:0] Select,
  output [7:0] Output
);

  wire [7:0] and_1_out;

  and and_1 (and_1_out[0], ~Select[0], ~Select[1], ~Select[2]);  // AND_Gate
  and and_2 (and_1_out[1], Select[0], ~Select[1], ~Select[2]);  // AND_Gate
  and and_3 (and_1_out[2], ~Select[0], Select[1], ~Select[2]);  // AND_Gate
  and and_4 (and_1_out[3], Select[0], Select[1], ~Select[2]);  // AND_Gate
  and and_5 (and_1_out[4], ~Select[0], ~Select[1], Select[2]);  // AND_Gate
  and and_6 (and_1_out[5], Select[0], ~Select[1], Select[2]);  // AND_Gate
  and and_7 (and_1_out[6], ~Select[0], Select[1], Select[2]);  // AND_Gate
  and and_8 (and_1_out[7], Select[0], Select[1], Select[2]);
  Pull_Resistor pull_resistor_1 (.node(Output));
  Transistor #(.\type ("n"), .width(8)) transistor_1 (.in(and_1_out), .out(Output), .gate(Enable));
endmodule
